# Fritzing sketch esp32-motion-detect (saved by Fritzing 0.9.6b)

parts:
  U1 = ESP32S-HiLetgo [part_number=ESP32S-HiLetgo]
  S1 = SWITCH-MOMENTARY-2 [package=tactile_switch_smd-2]
  10µF = Electrolytic Capacitor [capacitance=1µF voltage=35V package="100 mil [THT, electrolytic]"]
  PIR_(SR602) = Infrared Proximity Sensor

nets:
  N1: U1.3.3, PIR_(SR602).Vcc
  N2: U1.EN, 10µF.+
  N3: U1.GPIO12, PIR_(SR602).Vout
  GND: U1.GND, S1.2, 10µF.-, PIR_(SR602).GND

notes:
  Just for my board

custom parts:
  ESP32S-HiLetgo: HiLetgo ESP-WROOM-32 ESP32 ESP-32S Development Board 2.4GHz Dual-Mode WiFi + Bluetooth Dual Cores Microcontroller The ESP32 integrated with Antenna switches, RF Balun, power amplifiers, low-noise amplifiers, filters, and management modules, and the entire solution occupies the least area of PCB. 2.4 GHz Wi-Fi plus Bluetooth dual-mode chip, with TSMC Ultra-low power consumption 40nm technology,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
